// Logisim project A1 task 2 logisim.circ as structural Verilog: 1 circuit, main circuit main
module main (
  input  in_1,
  input  in_2,
  input  in_3,
  input  in_4,
  input  in_5,
  input  in_6,
  input  in_7,
  input  in_8,
  output out_9,
  output out_10,
  output out_11,
  output out_12
);

  wire adder_1_cout, xor_1_out;
  wire [3:0] adder_1_out;
  wire [3:3] not_1_out;

  Adder #(.width(4)) adder_1 (
    .a({in_1, in_2, in_3, in_4}), .b({in_5, in_6, in_7, in_8}), .out(adder_1_out), .cin(1'b0),
    .cout(adder_1_cout));
  xor xor_1 (xor_1_out, adder_1_out[3], adder_1_cout, in_5, in_1);
  not not_1 (not_1_out[3], adder_1_out[3]);
  Multiplexer #(.width(4), .enable("false")) multiplexer_1 (
    .in0(adder_1_out), .in1({not_1_out[3], {3{adder_1_out[3]}}}), .out({out_9, out_10, out_11, out_12}),
    .sel(xor_1_out));
endmodule
